# Fritzing sketch lampicka (saved by Fritzing 0.9.3b)
circuit board: 2.5996cm x 2.94932cm
breadboards: 1

parts:
  DISTANCE = female pin header, 4 pins [form="♀ (female)"]
  Espessif_Serial_Wifi_Modul_1 = ESP8266 ESP01 [part_number=ESP8266 package=THT]
  C1 = SMD Capacitor [package=1206]
  C2 = SMD Capacitor [package=1206]
  R2 = Resistor [tolerance=±5% resistance=4.7k package="1206 [SMD]"]
  R1 = Resistor [tolerance=±5% resistance=4.7k package="1206 [SMD]"]
  IC2 = Voltage Regulator LM1117 [package=sot223]
  Q2 = NPN-Transistor [package="TO92 [THT]"]
  Q3 = NPN-Transistor [package="TO92 [THT]"]
  Q1 = NPN-Transistor [package="TO92 [THT]"]
  Power_plug2 = Power plug

nets:
  12V: DISTANCE.pin1, C1.1, IC2.IN, Power_plug2.VCC
  N1: DISTANCE.pin2, Q2.C
  N2: DISTANCE.pin3, Q1.C
  N3: DISTANCE.pin4, Q3.C
  GND: Espessif_Serial_Wifi_Modul_1.GND, C1.2, C2.2, IC2.ADJ, Q2.E, Q3.E, Q1.E, Power_plug2.GND
  N4: Espessif_Serial_Wifi_Modul_1.RXD, Q2.B
  N5: Espessif_Serial_Wifi_Modul_1.TXD, Q3.B
  3.3V: Espessif_Serial_Wifi_Modul_1.VCC, Espessif_Serial_Wifi_Modul_1.GPIO16, Espessif_Serial_Wifi_Modul_1.CH_PD, C2.1, R2.Pin_1, R1.Pin_1, IC2.OUT
  N6: Espessif_Serial_Wifi_Modul_1.GPIO00, R1.Pin_0, Q1.B
  N7: Espessif_Serial_Wifi_Modul_1.GPIO02, R2.Pin_0

notes:
  G R B 12v

custom parts:
  ESP8266 ESP01: Generic WiFi Module based on the ESP8266 with onboard PCB antenna and UART communications
  SMD Capacitor: Capacitor Standard 0603 ceramic capacitor, and 0.1 leaded capacitor.
  Power plug: power plug
