# Fritzing sketch lampicka_addressable (saved by Fritzing 0.9.3b)
circuit board: 2.135cm x 1.89889cm
breadboards: 1

parts:
  Espessif_Serial_Wifi_Modul_1 = ESP8266 ESP01 [part_number=ESP8266 package=THT]
  C1 = SMD Capacitor [package=1206]
  C2 = SMD Capacitor [package=1206]
  R1 = Resistor [tolerance=±5% resistance=4.7k package="1206 [SMD]"]
  IC2 = Voltage Regulator LM1117 [package=sot223]
  Power_plug2 = Power plug
  LED = female alternating pin header, 1 pin [form="♀ (female)"]
  5V = female alternating pin header, 1 pin [form="♀ (female)"]
  R3 = Resistor [tolerance=±5% resistance=3.3 package="1206 [SMD]"]
  R2 = Resistor [tolerance=±5% resistance=4.7k package="1206 [SMD]"]
  GND = female alternating pin header, 1 pin [form="♀ (female)"]
  IR = female alternating pin header, 1 pin [form="♀ (female)"]
  3_3V = rounded female pin header, 1 pin [form="♀ (female rounded)"]
  GND_2 = female alternating pin header, 1 pin [form="♀ (female)"]
  Q1 = TRANSISTOR_NPN [package=sot23]
  433 = female alternating pin header, 1 pin [form="♀ (female)"]
  GND_3 = female alternating pin header, 1 pin [form="♀ (female)"]
  5V_2 = female alternating pin header, 1 pin [form="♀ (female)"]

nets:
  N1: Espessif_Serial_Wifi_Modul_1.GND, GND.pin1, GND_2.pin1, Q1.E, GND_3.pin1
  N2: Espessif_Serial_Wifi_Modul_1.RXD, LED.pin1
  N3: Espessif_Serial_Wifi_Modul_1.TXD, R3.Pin_0, Q1.C
  3.3V: Espessif_Serial_Wifi_Modul_1.VCC, Espessif_Serial_Wifi_Modul_1.GPIO16, Espessif_Serial_Wifi_Modul_1.CH_PD, C2.1, R1.Pin_1, IC2.OUT, R3.Pin_1, R2.Pin_1, 3_3V.pin1
  N4: Espessif_Serial_Wifi_Modul_1.GPIO00, R1.Pin_0
  N5: Espessif_Serial_Wifi_Modul_1.GPIO02, R2.Pin_0, IR.pin1
  5V: C1.1, IC2.IN, Power_plug2.VCC, 5V.pin1, 5V_2.pin1
  GND: C1.2, C2.2, IC2.ADJ, Power_plug2.GND
  N6: Q1.B, 433.pin1

custom parts:
  ESP8266 ESP01: Generic WiFi Module based on the ESP8266 with onboard PCB antenna and UART communications
  SMD Capacitor: Capacitor Standard 0603 ceramic capacitor, and 0.1 leaded capacitor.
  Power plug: power plug
